# Fritzing sketch sketch (saved by Fritzing 0.9.3b)
breadboards: 1

parts:
  Raspberry_Pi_1 = Raspberry Pi 3 [part_number=RPI-3-V1.2]
  U1 = Optocoupler [package=THT]
  R1 = Resistor [tolerance=±5% resistance=220 package=THT]
  Motherboard = male pin header, 2 pins [form="♂ (male)"]
  Button = Pushbutton [package="[SMD]"]

nets:
  N1: Raspberry_Pi_1.GPIO4, R1.Pin_1
  N2: Raspberry_Pi_1.GND, U1.Pin_2
  N3: U1.Pin_1, R1.Pin_0
  N4: U1.Pin_4, Motherboard.pin2, Button.Pin_1, Button.Pin_2
  N5: U1.Pin_5, Motherboard.pin1, Button.Pin_3, Button.Pin_4
